// Digital circuit timer.dig as structural Verilog
module timer (
  input  START,
  input  CLK,
  input  RST,
  input  clk_2,
  output RESET,
  output DIS,
  output [3:0] out_6,
  output [3:0] out_7,
  output [3:0] out_9
);

  wire comparator_1_eq, comparator_2_eq, comparator_3_gt, comparator_3_lt, not_1_out;

  not not_1 (not_1_out, RST);
  // upcounter upcounter_1: pin names not known; wires that end beside it: CLK, START, not_1_out, 4'b0000, clk_2, out_6
  Comparator #(.Bits(4)) comparator_1 (.a(4'b1111), .b(out_6), .eq(comparator_1_eq));  // open: gt, lt
  // upcounter upcounter_2: pin names not known; wires that end beside it: comparator_1_eq, not_1_out, 4'b0000, clk_2, out_7
  Comparator #(.Bits(4)) comparator_2 (.a(4'b1111), .b(out_7), .eq(comparator_2_eq));  // open: gt, lt
  // upcounter upcounter_3: pin names not known; wires that end beside it: comparator_2_eq, not_1_out, 4'b0000, clk_2, out_9
  Comparator #(.Bits(12)) comparator_3 (
    .a(12'h12c), .b({out_9, out_7, out_6}), .gt(comparator_3_gt), .eq(RESET), .lt(comparator_3_lt));
  LED led_1 (.in(comparator_3_gt));
  LED led_2 (.in(comparator_3_lt));

  assign DIS = START;

  // Notes on the sheet:
  //   clk_2: Hz: 100
endmodule
